# Fritzing sketch UniversalIRRemoteControl-v2 (saved by Fritzing 0.9.6b)

parts:
  WeMos_D1_Mini1 = WeMos D1 Mini
  IR3 = vs1838b [package=THT]
  R4 = Resistor [tolerance=±5% resistance=22 package="0402 [SMD]"]
  C3 = Capacitor Polarized [part_number="10 µF" package=panasonic_c]
  C2 = Capacitor Polarized [part_number="10 µF" package=panasonic_c]
  Q1 = TRANSISTOR_NPN [part_number=S8050 package=to-92-ammo]
  D2 = LTE-302 [part_number=TSFF5210 package=lte-302]
  U5 = ESP-12F (ESP8266 WiFi Module) [part_number=ESP8266]
  AMS2 = SOT-223 [part_number=AMS1117 package=SOT-223]
  U4 = USB connector [package=THT]
  S1 = Momentary Switch [package=ksa_sealed_tac_switch]
  Button3 = male pin header, 3 pins [form="♂ (male)"]
  Button1 = male pin header, 3 pins [form="♂ (male)"]
  TRS2 = Audio Jack (TRS) 3.5mm [package="PG203J [THT]"]

nets:
  N1: WeMos_D1_Mini1.3V3, IR3.Vs
  N2: WeMos_D1_Mini1.D4, IR3.Data
  N3: WeMos_D1_Mini1.G, IR3.GND
  N4: R4.Pin_0, Q1.E
  N5: R4.Pin_1, D2.A, TRS2.Tip
  VIN: C3.+, Q1.C, AMS2.Vin, U4.5V, U4.d+, Button3.pin1
  GND: C3.-, C2.-, D2.C, U5.GND, U5.TXD0, U5.GPIO15, AMS2.GND/Adjust, U4.GND, U4.chassis5, U4.chassis6, S1.3, Button1.pin2, Button1.pin3, TRS2.Sleeve
  N6: C2.+, U5.VCC, U5.EN, AMS2.Vout, Button1.pin1
  N7: Q1.B, U5.GPIO13
  N8: U5.RXD0, Button3.pin3
  N9: U5.GPIO0, S1.2

notes:
  Receptor
  IR LED: 1,5V @ 100 mA
  Resistor: 12-15 Ω
  3V3
  5V
  D G V
  D4 = GPIO2
  PGM
  RxD
  TxD

custom parts:
  ESP-12F (ESP8266 WiFi Module): WiFi Module based on the ESP8266 with onboard PCB antenna and UART communications
  SOT-223: Top view SOT-223 package.
