# Fritzing sketch UniversalIRRemoteControl (saved by Fritzing 0.9.6b)

parts:
  U1 = ESP8266 WiFi Module [part_number=ESP8266]
  Q1 = TRANSISTOR_NPN [part_number=S8050 package=to-92-ammo]
  P2 = S1133 Si Photodiode [part_number=BPV10NF package="8mm Ceramic [THT]"]
  D2 = LTE-302 [part_number=TSFF5210 package=lte-302]
  R4 = Resistor [tolerance=±5% resistance=22 package="0402 [SMD]"]
  R5 = Resistor [tolerance=±5% resistance=220k package="0402 [SMD]"]
  IC2 = Voltage Regulator LM1117 [package=sot223]
  U4 = USB connector [package=THT]
  C2 = Capacitor Polarized [part_number="10 µF" package=panasonic_c]
  C3 = Capacitor Polarized [part_number="10 µF" package=panasonic_c]

nets:
  N1: U1.VCC, U1.CH_PD, R5.Pin_0, IC2.OUT, C2.+
  N2: U1.GND, P2.anode, R4.Pin_1, IC2.ADJ, U4.chassis6, C2.-, C3.-
  N3: U1.GPIO_5, P2.cathode, R5.Pin_1
  N4: U1.GPIO_13, Q1.B
  N5: Q1.E, D2.A
  N6: Q1.C, IC2.IN, U4.5V, C3.+
  N7: D2.C, R4.Pin_0

notes:
  IR LED: 1,5V @ 100 mA
  Resistor: 12-15 Ω
  IR Photodiode: 30-60 µA
  Resistor: 110-55 kΩ 220 kΩ
  5V
  3V3
